// Digital circuit clockctrl.dig as structural Verilog
module clockctrl (
  input  clock,
  input  step,
  input  run,
  output stall
);

  wire and_1_out, d_ff_1_q, d_ff_2_nq, or_1_out, rs_ff_as_1_q;

  D_FF d_ff_1 (.D(step), .C(clock), .Q(d_ff_1_q));  // open: nQ
  D_FF d_ff_2 (.D(d_ff_1_q), .C(clock), .nQ(d_ff_2_nq));  // open: Q
  and and_1 (and_1_out, d_ff_1_q, d_ff_2_nq);
  RS_FF_AS rs_ff_as_1 (.S(run), .R(and_1_out), .Q(rs_ff_as_1_q));  // open: nQ
  or or_1 (or_1_out, rs_ff_as_1_q, and_1_out);
  D_FF d_ff_3 (.D(or_1_out), .C(clock), .nQ(stall));  // open: Q

  // Notes on the sheet:
  //   clock: Hz: 10
endmodule
