// Digital circuit decoder.dig as structural Verilog
module decoder (
  input  [15:0] rdval,
  input  [15:0] rsval,
  input  [15:0] instr,
  output [1:0] rs,
  output [1:0] rd,
  output [15:0] L,
  output [15:0] R,
  output [4:0] op,
  output tworeg,
  output rs_valid,
  output rd_valid,
  output jump
);

  wire imm11_valid, sys;
  wire [3:2] multiplexer_1_out, multiplexer_2_out;
  wire [4:0] op_raw;
  wire [15:0] imm5, imm11, multiplexer_4_out, multiplexer_5_out;

  BitExtender #(.inputBits(5)) bitextender_1 (.in(instr[15:11]), .out(imm5));
  BitExtender #(.inputBits(11)) bitextender_2 (.in(instr[15:5]), .out(imm11));
  instdecoder instdecoder_1 (
    .fmt(instr[2:0]), .op1(instr[4:3]), .op2(instr[10:7]), .op3(instr[15:11]), .op(op_raw), .tworeg(tworeg),
    .sys(sys), .imm11_valid(imm11_valid), .rs_valid(rs_valid), .rd_valid(rd_valid));  // open: imm5_valid
  Multiplexer #(.Bits(4)) multiplexer_1 (
    .sel(rs_valid), .in_0(4'b0000), .in_1(instr[10:7]), .out({multiplexer_1_out, rs}));
  Multiplexer #(.Bits(4)) multiplexer_2 (
    .sel(rd_valid), .in_0(4'b0000), .in_1(instr[6:3]), .out({multiplexer_2_out, rd}));
  Multiplexer #(.Bits(5)) multiplexer_3 (.sel(sys), .in_0(op_raw), .in_1(5'b01000), .out(op));
  Multiplexer #(.Bits(16)) multiplexer_4 (.sel(imm11_valid), .in_0(imm5), .in_1(imm11), .out(multiplexer_4_out));
  Multiplexer #(.Bits(16)) multiplexer_5 (.sel(rs_valid), .in_0({16{1'b0}}), .in_1(rsval), .out(multiplexer_5_out));
  Multiplexer #(.Bits(16)) multiplexer_6 (.sel(tworeg), .in_0(multiplexer_4_out), .in_1(multiplexer_5_out), .out(R));
  and and_1 (jump, op[2], ~op[3], ~op[4]);  // And

  assign L = rdval;

  // Other names for the same wires on the sheet: fmt[2:0] = instr[2:0]; op1[1:0] = instr[4:3]; rd_t[3:0] = instr[6:3];
  //   op2[3:0] = instr[10:7]; rs_t[3:0] = instr[10:7]; op3[4:0] = instr[15:11]
endmodule

/* Test case ls:
instr               rsval rs rdval rd L R op jump
0b0000000000000100  5     0  0     0  0 0 0  0
0b0000000000000101  5     0  0     0  0 0 1  0
0b0000000000000111  5     0  0     0  0 0 3  0
0b0000000000011101  5     0  9     3  9 0 1  0
0b0011100100011101  5     2  9     3  9 7 1  0
*/

/* Test case rr:
instr               rsval rs rdval rd L R op jump
0b0000000000000010  5     0  2     0  2 5 0  0
0b1111100000011010  5     0  2     3  2 5 31 0
0b1000000110011010  5     3  2     3  2 5 16 0
*/

/* Test case i11:
instr               rsval rs rdval rd L R      op       jump 
0b0000000000000001  5     0  2     0  2 0      0b00100  1    
0b0000000000011001  5     0  2     0  2 0      0b00111  1    
0b0100000000111001  5     0  2     0  2 0x201  0b00111  1    
0b1111111110111001  5     0  2     0  2 0xFFFD 0b00111  1    


0b0000000000000000  5     0  2     0  2 0      8        0    
0b0000000000011000  5     0  2     0  2 0      8        0    
0b0100000000111000  5     0  2     0  2 0x201  8        0    
0b1111111110111000  5     0  2     0  2 0xFFFD 8        0    
*/

/* Test case ri:
instr               rsval rs rdval rd L R      op       jump
0b0000000000000011  5     0  2     0  2 0      0b10000  0
0b0000000100011011  5     0  2     3  2 0      0b10010  0
0b1000100100011011  5     0  2     3  2 0xfff1 0b10010  0
0b0100100100011011  5     0  2     3  2 9      0b10010  0
*/
