// Digital circuit execute.dig as structural Verilog
module execute (
  input  [15:0] L,
  input  [15:0] R,
  input  [2:0] cond,
  input  [2:0] op,
  output [15:0] result,
  output skip_n
);

  wire add_1_c_o, and_1_out, and_2_out, and_3_out, and_4_out, and_5_out, and_6_out, eq, eq_eq, ge, hs, lo,
       lt, ne, not_2_out, not_3_out, or_1_out, signed_eq, signed_gt, signed_lt;
  wire [15:0] add_1_s, multiplexer_1_out, not_1_out, xor_1_out;

  Decoder #(.Selector_Bits(3)) decoder_1 (
    .sel(cond), .out_1(eq), .out_2(ne), .out_3(lt), .out_4(ge), .out_5(lo), .out_6(hs));  // open: out_0, out_7
  Multiplexer #(.Bits(16)) multiplexer_1 (.sel(op[2]), .in_0(R), .in_1(not_1_out), .out(multiplexer_1_out));
  assign not_1_out = ~R;  // Not not_1, 16 bits wide
  Add #(.Bits(16)) add_1 (.a(L), .b(multiplexer_1_out), .c_i(op[2]), .s(add_1_s), .c_o(add_1_c_o));
  assign xor_1_out = L ^ R;  // XOr xor_1, 16 bits wide
  Comparator #(.Bits(16)) u_eq (.a(xor_1_out), .b({16{1'b0}}), .eq(eq_eq));  // open: gt, lt
  Comparator #(.Signed("true"), .Bits(16)) \signed  (.a(L), .b(R), .gt(signed_gt), .eq(signed_eq), .lt(signed_lt));
  or or_1 (or_1_out, signed_gt, signed_eq);
  not not_2 (not_2_out, add_1_c_o);
  not not_3 (not_3_out, eq_eq);
  Multiplexer #(.Selector_Bits(2), .Bits(16)) multiplexer_2 (
    .sel(op[1:0]), .in_0(L), .in_1(add_1_s), .in_2({16{1'b0}}), .in_3(multiplexer_1_out), .out(result));
  and and_1 (and_1_out, lt, or_1_out);
  and and_2 (and_2_out, ge, signed_lt);
  and and_3 (and_3_out, lo, add_1_c_o);
  and and_4 (and_4_out, hs, not_2_out);
  and and_5 (and_5_out, ne, eq_eq);
  and and_6 (and_6_out, eq, not_3_out);
  or or_2 (skip_n, and_1_out, and_2_out, and_3_out, and_4_out, and_5_out, and_6_out);
endmodule
