// Digital circuit fetch.dig as structural Verilog
module fetch (
  input  prog,
  input  [31:0] bypass,
  input  [31:0] instr_i,
  input  clock,
  input  [15:0] value,
  input  jump,
  output [3:0] pc,
  output [31:0] instr_o
);

  Multiplexer #(.Bits(32)) multiplexer_1 (.sel(prog), .in_0(instr_i), .in_1(bypass), .out(instr_o));
  CounterPreset #(.Bits(4), .isProgramCounter("true")) u_PC (
    .en(1'b1), .C(clock), .dir(1'b0), .in(value[3:0]), .ld(jump), .clr(1'b0), .out(pc));  // open: ovf
  // Pins of 1 and 32 bits meet at instr_o
endmodule
