// Digital circuit frontpanel.dig as structural Verilog
module frontpanel (
  input  clock,
  input  erun,
  input  DC,
  output [15:0] R0,
  output [15:0] R1,
  output [15:0] R2,
  output [15:0] R3,
  output [15:0] PC,
  output halt,
  output error,
  output [15:0] R4,
  output [15:0] R5,
  output [15:0] R6,
  output [15:0] R7
);

  wire aluopdisplay_1_p1, aluopdisplay_1_p2, busdisplay_1_p1, busdisplay_1_p2, busdisplay_1_p3,
       busdisplay_1_p4, busdisplay_1_p5, busdisplay_2_p1, busdisplay_2_p2, busdisplay_2_p3, busdisplay_2_p4,
       busdisplay_2_p5, busdisplay_3_p1, busdisplay_3_p2, busdisplay_3_p3, busdisplay_3_p4, busdisplay_3_p5,
       busdisplay_4_p1, busdisplay_4_p2, busdisplay_4_p3, busdisplay_4_p4, busdisplay_4_p5, d_ff_1_q,
       debugreg_2_p1, dipswitch_1_out, hex, instrdisplay_1_p3, instrdisplay_1_p6, instrdisplay_1_p8,
       instrdisplay_1_p10, instrdisplay_1_p12, instrdisplay_1_p14, MC, rddisplay_1_p1, rddisplay_1_p2,
       rddisplay_1_p3, rddisplay_2_p1, rddisplay_2_p2, rddisplay_2_p3, rddisplay_3_p1, rddisplay_3_p2,
       rddisplay_3_p3, run_t, skip, slow_t, stalled_t, step_t, undriven;
  wire [3:0] busdisplay_1_d1, busdisplay_1_d2, busdisplay_1_d3, busdisplay_1_d4, busdisplay_1_d5,
       busdisplay_2_d1, busdisplay_2_d2, busdisplay_2_d3, busdisplay_2_d4, busdisplay_2_d5, busdisplay_3_d1,
       busdisplay_3_d2, busdisplay_3_d3, busdisplay_3_d4, busdisplay_3_d5, busdisplay_4_d1, busdisplay_4_d2,
       busdisplay_4_d3, busdisplay_4_d4, busdisplay_4_d5;
  wire [7:0] rj32_1_a_prog;
  wire [13:0] undriven_3;
  wire [15:0] aluopdisplay_1_d1, aluopdisplay_1_d2, Data_d, instrdisplay_1_p2, instrdisplay_1_p5,
       instrdisplay_1_p7, instrdisplay_1_p9, instrdisplay_1_p11, instrdisplay_1_p13, Program_d,
       rddisplay_1_d1, rddisplay_1_d2, rddisplay_1_d3, rddisplay_2_d1, rddisplay_2_d2, rddisplay_2_d3,
       rddisplay_3_d1, rddisplay_3_d2, rddisplay_3_d3, undriven_2;
  wire [25:0] aluopdisplay_1_o, busdisplay_1_o, busdisplay_2_o, db, debugreg_2_p4, instrdisplay_1_p15,
       rddisplay_1_o, rddisplay_2_o, rddisplay_3_o, undriven_4, undriven_5, undriven_6, undriven_7,
       undriven_8, undriven_9;

  Button step (.out(step_t));
  Button slow (.out(slow_t));
  Button run (.out(run_t));
  LED stalled (.in(stalled_t));
  BlockRAMDualPort #(.AddrBits(8), .isProgramMemory("true"), .Bits(16)) Program (
    .A(rj32_1_a_prog), .Din({16{1'b0}}), .str(1'b0), .C(MC), .D(Program_d));
  SixteenSeg sixteenseg_1 (.led(rddisplay_1_d1), .dp(rddisplay_1_p1));
  rddisplay rddisplay_1 (
    .D1(rddisplay_1_d1), .P1(rddisplay_1_p1), .D2(rddisplay_1_d2), .P2(rddisplay_1_p2), .D3(rddisplay_1_d3),
    .P3(rddisplay_1_p3), .i(db), .o(rddisplay_1_o), .C(1'b0));
  rj32 rj32_1 (
    .stall(stalled_t), .skip(skip), .halt(halt), .error(error), .db(db), .erun(erun), .run_faster(1'b1),
    .run_fast(run_t), .run_slow(slow_t), .step(step_t), .clock(clock), .A_prog(rj32_1_a_prog),
    .D_out(Program_d));  // open: clock_m, D_prog, w_en, A_data, D_in
  SixteenSeg sixteenseg_2 (.led(instrdisplay_1_p2), .dp(instrdisplay_1_p3));
  SixteenSeg sixteenseg_3 (.led(instrdisplay_1_p5), .dp(instrdisplay_1_p6));
  // instrdisplay instrdisplay_1: pin names not known; wires that end beside it: db, instrdisplay_1_p2, instrdisplay_1_p3, MC, instrdisplay_1_p5, instrdisplay_1_p6, instrdisplay_1_p7, instrdisplay_1_p8, instrdisplay_1_p9, instrdisplay_1_p10, instrdisplay_1_p11, instrdisplay_1_p12, instrdisplay_1_p13, instrdisplay_1_p14, instrdisplay_1_p15
  SixteenSeg sixteenseg_4 (.led(rddisplay_1_d2), .dp(rddisplay_1_p2));
  SixteenSeg sixteenseg_5 (.led(rddisplay_1_d3), .dp(rddisplay_1_p3));
  SixteenSeg sixteenseg_6 (.led(instrdisplay_1_p7), .dp(instrdisplay_1_p8));
  SixteenSeg sixteenseg_7 (.led(instrdisplay_1_p9), .dp(instrdisplay_1_p10));
  Seven_Seg_Hex seven_seg_hex_1 (.d(busdisplay_1_d1), .dp(busdisplay_1_p1));
  busdisplay busdisplay_1 (
    .D1(busdisplay_1_d1), .P1(busdisplay_1_p1), .D2(busdisplay_1_d2), .P2(busdisplay_1_p2),
    .D3(busdisplay_1_d3), .P3(busdisplay_1_p3), .D4(busdisplay_1_d4), .P4(busdisplay_1_p4),
    .D5(busdisplay_1_d5), .P5(busdisplay_1_p5), .i(rddisplay_1_o), .o(busdisplay_1_o), .C(2'b11), .H(hex));
  SixteenSeg sixteenseg_8 (.led(instrdisplay_1_p11), .dp(instrdisplay_1_p12));
  SixteenSeg sixteenseg_9 (.led(instrdisplay_1_p13), .dp(instrdisplay_1_p14));
  Seven_Seg_Hex seven_seg_hex_2 (.d(busdisplay_1_d2), .dp(busdisplay_1_p2));
  Seven_Seg_Hex seven_seg_hex_3 (.d(busdisplay_1_d3), .dp(busdisplay_1_p3));
  BlockRAMDualPort #(.AddrBits(14), .Bits(16)) Data (
    .A(undriven_3), .Din(undriven_2), .str(undriven), .C(clock), .D(Data_d));
  SixteenSeg sixteenseg_10 (.led(rddisplay_2_d1), .dp(rddisplay_2_p1));
  Seven_Seg_Hex seven_seg_hex_4 (.d(busdisplay_1_d4), .dp(busdisplay_1_p4));
  Seven_Seg_Hex seven_seg_hex_5 (.d(busdisplay_1_d5), .dp(busdisplay_1_p5));
  D_FF d_ff_1 (.D(debugreg_2_p1), .C(clock), .Q(d_ff_1_q));  // open: nQ
  SixteenSeg sixteenseg_11 (.led(rddisplay_2_d2), .dp(rddisplay_2_p2));
  SixteenSeg sixteenseg_12 (.led(rddisplay_2_d3), .dp(rddisplay_2_p3));
  rddisplay rddisplay_2 (
    .D1(rddisplay_2_d1), .P1(rddisplay_2_p1), .D2(rddisplay_2_d2), .P2(rddisplay_2_p2), .D3(rddisplay_2_d3),
    .P3(rddisplay_2_p3), .i(instrdisplay_1_p15), .o(rddisplay_2_o), .C(1'b0));
  Seven_Seg_Hex seven_seg_hex_6 (.d(busdisplay_2_d1), .dp(busdisplay_2_p1));
  busdisplay busdisplay_2 (
    .D1(busdisplay_2_d1), .P1(busdisplay_2_p1), .D2(busdisplay_2_d2), .P2(busdisplay_2_p2),
    .D3(busdisplay_2_d3), .P3(busdisplay_2_p3), .D4(busdisplay_2_d4), .P4(busdisplay_2_p4),
    .D5(busdisplay_2_d5), .P5(busdisplay_2_p5), .i(busdisplay_1_o), .o(busdisplay_2_o), .C(2'b01), .H(hex));
  SixteenSeg sixteenseg_13 (.led(rddisplay_3_d1), .dp(rddisplay_3_p1));
  DipSwitch u_hex (.out(hex));
  Seven_Seg_Hex seven_seg_hex_7 (.d(busdisplay_2_d2), .dp(busdisplay_2_p2));
  Seven_Seg_Hex seven_seg_hex_8 (.d(busdisplay_2_d3), .dp(busdisplay_2_p3));
  SixteenSeg sixteenseg_14 (.led(rddisplay_3_d2), .dp(rddisplay_3_p2));
  SixteenSeg sixteenseg_15 (.led(rddisplay_3_d3), .dp(rddisplay_3_p3));
  rddisplay rddisplay_3 (
    .D1(rddisplay_3_d1), .P1(rddisplay_3_p1), .D2(rddisplay_3_d2), .P2(rddisplay_3_p2), .D3(rddisplay_3_d3),
    .P3(rddisplay_3_p3), .i(rddisplay_2_o), .o(rddisplay_3_o), .C(1'b1));
  Seven_Seg_Hex seven_seg_hex_9 (.d(busdisplay_2_d4), .dp(busdisplay_2_p4));
  Seven_Seg_Hex seven_seg_hex_10 (.d(busdisplay_2_d5), .dp(busdisplay_2_p5));
  DipSwitch dipswitch_1 (.out(dipswitch_1_out));
  Seven_Seg_Hex seven_seg_hex_11 (.d(busdisplay_3_d1), .dp(busdisplay_3_p1));
  SixteenSeg sixteenseg_16 (.led(aluopdisplay_1_d1), .dp(aluopdisplay_1_p1));
  aluopdisplay aluopdisplay_1 (
    .D1(aluopdisplay_1_d1), .P1(aluopdisplay_1_p1), .D2(aluopdisplay_1_d2), .P2(aluopdisplay_1_p2),
    .i(busdisplay_2_o), .o(aluopdisplay_1_o));
  debugreg debugreg_1 (.i(db), .s(8'h17), .v(PC), .o(debugreg_2_p4));
  // debugreg debugreg_2: pin names not known; wires that end beside it: debugreg_2_p1, d_ff_1_q, {8{1'b0}}, debugreg_2_p4, R0
  // vga_frontpanel vga_frontpanel_1: pin names not known; wires that end beside it: DC, dipswitch_1_out, db
  Seven_Seg_Hex seven_seg_hex_12 (.d(busdisplay_3_d2), .dp(busdisplay_3_p2));
  Seven_Seg_Hex seven_seg_hex_13 (.d(busdisplay_3_d3), .dp(busdisplay_3_p3));
  busdisplay busdisplay_3 (
    .D1(busdisplay_3_d1), .P1(busdisplay_3_p1), .D2(busdisplay_3_d2), .P2(busdisplay_3_p2),
    .D3(busdisplay_3_d3), .P3(busdisplay_3_p3), .D4(busdisplay_3_d4), .P4(busdisplay_3_p4),
    .D5(busdisplay_3_d5), .P5(busdisplay_3_p5), .i(rddisplay_3_o), .C(2'b00), .H(hex));  // open: o
  SixteenSeg sixteenseg_17 (.led(aluopdisplay_1_d2), .dp(aluopdisplay_1_p2));
  Seven_Seg_Hex seven_seg_hex_14 (.d(busdisplay_3_d4), .dp(busdisplay_3_p4));
  Seven_Seg_Hex seven_seg_hex_15 (.d(busdisplay_3_d5), .dp(busdisplay_3_p5));
  Seven_Seg_Hex seven_seg_hex_16 (.d(busdisplay_4_d1), .dp(busdisplay_4_p1));
  Seven_Seg_Hex seven_seg_hex_17 (.d(busdisplay_4_d2), .dp(busdisplay_4_p2));
  busdisplay busdisplay_4 (
    .D1(busdisplay_4_d1), .P1(busdisplay_4_p1), .D2(busdisplay_4_d2), .P2(busdisplay_4_p2),
    .D3(busdisplay_4_d3), .P3(busdisplay_4_p3), .D4(busdisplay_4_d4), .P4(busdisplay_4_p4),
    .D5(busdisplay_4_d5), .P5(busdisplay_4_p5), .i(aluopdisplay_1_o), .C(2'b10), .H(hex));  // open: o
  Seven_Seg_Hex seven_seg_hex_18 (.d(busdisplay_4_d3), .dp(busdisplay_4_p3));
  Seven_Seg_Hex seven_seg_hex_19 (.d(busdisplay_4_d4), .dp(busdisplay_4_p4));
  Seven_Seg_Hex seven_seg_hex_20 (.d(busdisplay_4_d5), .dp(busdisplay_4_p5));
  debugreg debugreg_3 (.i(db), .s(8'h1), .v(R1), .o(undriven_4));
  debugreg debugreg_4 (.i(undriven_4), .s(8'h2), .v(R2), .o(undriven_5));
  debugreg debugreg_5 (.i(undriven_5), .s(8'h3), .v(R3), .o(undriven_6));
  debugreg debugreg_6 (.i(undriven_6), .s(8'h4), .v(R4), .o(undriven_7));
  debugreg debugreg_7 (.i(undriven_7), .s(8'h5), .v(R5), .o(undriven_8));
  debugreg debugreg_8 (.i(undriven_8), .s(8'h6), .v(R6), .o(undriven_9));
  debugreg debugreg_9 (.i(undriven_9), .s(8'h7), .v(R7));  // open: o
  LED u_skip (.in(skip));

  // Other names for the same wires on the sheet: C = clock

  // Notes on the sheet:
  //   clock: Hz: 800
  //   DC: Hz: 2147483647
  //   rj45 Creates
  //   =
endmodule
