// Digital circuit instrdisplay.dig as structural Verilog
module instrdisplay (
  input  [33:0] i,
  output [15:0] D1,
  output P1,
  output [15:0] D2,
  output P2,
  output [15:0] D3,
  output P3,
  output [15:0] D4,
  output P4,
  output [15:0] D5,
  output P5,
  output [15:0] D6,
  output P6,
  output [33:0] o
);

  wire [4:0] ctrlbreakout_1_p2;
  wire [6:0] op2ascii_1_l0, op2ascii_1_l1, op2ascii_1_l2, op2ascii_1_l3, op2ascii_1_l4, op2ascii_1_l5;

  // ctrlbreakout ctrlbreakout_1: pin names not known; wires that end beside it: i, ctrlbreakout_1_p2
  ROM #(.AddrBits(7), .Bits(16)) ASCII (.A(op2ascii_1_l0), .sel(1'b1), .D(D1));
  ROM #(.AddrBits(7), .Bits(16)) ASCII_2 (.A(op2ascii_1_l1), .sel(1'b1), .D(D2));
  ROM #(.AddrBits(7), .Bits(16)) ASCII_3 (.A(op2ascii_1_l2), .sel(1'b1), .D(D3));
  op2ascii op2ascii_1 (
    .I(ctrlbreakout_1_p2), .L0(op2ascii_1_l0), .L1(op2ascii_1_l1), .L2(op2ascii_1_l2), .L3(op2ascii_1_l3),
    .L4(op2ascii_1_l4), .L5(op2ascii_1_l5));
  // Probe op on ctrlbreakout_1_p2
  ROM #(.AddrBits(7), .Bits(16)) ASCII_4 (.A(op2ascii_1_l3), .sel(1'b1), .D(D4));
  ROM #(.AddrBits(7), .Bits(16)) ASCII_5 (.A(op2ascii_1_l4), .sel(1'b1), .D(D5));
  ROM #(.AddrBits(7), .Bits(16)) ASCII_6 (.A(op2ascii_1_l5), .sel(1'b1), .D(D6));

  assign o = i;
  assign P1 = 1'b0;
  assign P2 = 1'b0;
  assign P3 = 1'b0;
  assign P4 = 1'b0;
  assign P5 = 1'b0;
  assign P6 = 1'b0;

  // Notes on the sheet:
  //   contents of ASCII (hex, n*v repeats v):
  //   90ff,c,377,33f,38c,3bb,3fb,f,3ff,3bf,3cf,4a3f,f3,483f,3f3,1c3,0,0,0,0,0,0,0,0,0,0,
  //   0,0,0,0,0,0,0,0,0,0,0,0,0,0,0,0,0,0,0,0,0,0,90ff,c,377,33f,38c,3bb,3fb,f,3ff,3bf,
  //   0,0,0,0,0,0,0,3cf,4a3f,f3,483f,3f3,1c3,2fb,3cc,4833,7c,31c0,f0,14cc,24cc,ff,3c7,20ff,
  //   23c7,3bb,4803,fc,90c0,a0cc,b400,5400,9033
  //   contents of ASCII_2 (hex, n*v repeats v):
  //   90ff,c,377,33f,38c,3bb,3fb,f,3ff,3bf,3cf,4a3f,f3,483f,3f3,1c3,0,0,0,0,0,0,0,0,0,0,
  //   0,0,0,0,0,0,0,0,0,0,0,0,0,0,0,0,0,0,0,0,0,0,90ff,c,377,33f,38c,3bb,3fb,f,3ff,3bf,
  //   0,0,0,0,0,0,0,3cf,4a3f,f3,483f,3f3,1c3,2fb,3cc,4833,7c,31c0,f0,14cc,24cc,ff,3c7,20ff,
  //   23c7,3bb,4803,fc,90c0,a0cc,b400,5400,9033
  //   contents of ASCII_3 (hex, n*v repeats v):
  //   90ff,c,377,33f,38c,3bb,3fb,f,3ff,3bf,3cf,4a3f,f3,483f,3f3,1c3,0,0,0,0,0,0,0,0,0,0,
  //   0,0,0,0,0,0,0,0,0,0,0,0,0,0,0,0,0,0,0,0,0,0,90ff,c,377,33f,38c,3bb,3fb,f,3ff,3bf,
  //   0,0,0,0,0,0,0,3cf,4a3f,f3,483f,3f3,1c3,2fb,3cc,4833,7c,31c0,f0,14cc,24cc,ff,3c7,20ff,
  //   23c7,3bb,4803,fc,90c0,a0cc,b400,5400,9033
  //   contents of ASCII_4 (hex, n*v repeats v):
  //   90ff,c,377,33f,38c,3bb,3fb,f,3ff,3bf,3cf,4a3f,f3,483f,3f3,1c3,0,0,0,0,0,0,0,0,0,0,
  //   0,0,0,0,0,0,0,0,0,0,0,0,0,0,0,0,0,0,0,0,0,0,90ff,c,377,33f,38c,3bb,3fb,f,3ff,3bf,
  //   0,0,0,0,0,0,0,3cf,4a3f,f3,483f,3f3,1c3,2fb,3cc,4833,7c,31c0,f0,14cc,24cc,ff,3c7,20ff,
  //   23c7,3bb,4803,fc,90c0,a0cc,b400,5400,9033
  //   contents of ASCII_5 (hex, n*v repeats v):
  //   90ff,c,377,33f,38c,3bb,3fb,f,3ff,3bf,3cf,4a3f,f3,483f,3f3,1c3,0,0,0,0,0,0,0,0,0,0,
  //   0,0,0,0,0,0,0,0,0,0,0,0,0,0,0,0,0,0,0,0,0,0,90ff,c,377,33f,38c,3bb,3fb,f,3ff,3bf,
  //   0,0,0,0,0,0,0,3cf,4a3f,f3,483f,3f3,1c3,2fb,3cc,4833,7c,31c0,f0,14cc,24cc,ff,3c7,20ff,
  //   23c7,3bb,4803,fc,90c0,a0cc,b400,5400,9033
  //   contents of ASCII_6 (hex, n*v repeats v):
  //   90ff,c,377,33f,38c,3bb,3fb,f,3ff,3bf,3cf,4a3f,f3,483f,3f3,1c3,0,0,0,0,0,0,0,0,0,0,
  //   0,0,0,0,0,0,0,0,0,0,0,0,0,0,0,0,0,0,0,0,0,0,90ff,c,377,33f,38c,3bb,3fb,f,3ff,3bf,
  //   0,0,0,0,0,0,0,3cf,4a3f,f3,483f,3f3,1c3,2fb,3cc,4833,7c,31c0,f0,14cc,24cc,ff,3c7,20ff,
  //   23c7,3bb,4803,fc,90c0,a0cc,b400,5400,9033
endmodule
