// Digital circuit memaccess.dig as structural Verilog
module memaccess (
  input  [15:0] result,
  input  [15:0] rdval,
  input  store,
  input  en,
  output [15:0] A,
  output str,
  output [15:0] D_in
);

  and and_1 (str, store, en);
  // Pins of 14 and 16 bits meet at result

  assign A = result;
  assign D_in = rdval;
endmodule
