// Digital circuit engine.dig as structural Verilog
module engine (
  input  [11:0] x_i,
  input  [11:0] y_i,
  input  line,
  input  frame,
  input  hsync_i,
  input  vsync_i,
  input  en_disp_i,
  input  clk,
  input  rst,
  output [11:0] x_o,
  output [11:0] y_o,
  output [7:0] r,
  output [7:0] g,
  output [7:0] b,
  output hsync_o,
  output vsync_o,
  output en_disp_o
);

  wire draw_1_en_disp_o, draw_1_hsync_o, draw_1_vsync_o;
  wire [11:0] draw_1_x_o, draw_1_y_o;

  draw draw_1 (
    .x_i(x_i), .y_i(y_i), .hsync_i(hsync_i), .vsync_i(vsync_i), .en_disp_i(en_disp_i), .line(line),
    .frame(frame), .clk(clk), .rst(rst), .x_o(draw_1_x_o), .y_o(draw_1_y_o), .hsync_o(draw_1_hsync_o),
    .vsync_o(draw_1_vsync_o), .en_disp_o(draw_1_en_disp_o));
  scanout scanout_1 (
    .x_i(draw_1_x_o), .y_i(draw_1_y_o), .hsync_i(draw_1_hsync_o), .vsync_i(draw_1_vsync_o),
    .en_disp_i(draw_1_en_disp_o), .clk(clk), .rst(rst), .x_o(x_o), .y_o(y_o), .r(r), .g(g), .b(b),
    .hsync_o(hsync_o), .vsync_o(vsync_o), .en_disp_o(en_disp_o));

  // Other names for the same wires on the sheet: C = clk; R_t = rst
endmodule
