// Digital circuit vdp.dig as structural Verilog
module vdp (
  input  clk,
  input  rst,
  input  [11:0] hfp,
  input  [11:0] hsn,
  input  [11:0] hbp,
  input  [11:0] httl,
  input  hneg,
  input  [11:0] vfp,
  input  [11:0] vsn,
  input  [11:0] vbp,
  input  [11:0] vttl,
  input  vneg,
  output [7:0] R,
  output [7:0] G,
  output [7:0] B,
  output hs,
  output vs,
  output de,
  output [11:0] X,
  output [11:0] Y,
  output nl,
  output nf
);

  wire scanxy_1_p6, scanxy_1_p7, scanxy_1_p8, scanxy_1_p9, scanxy_1_p10, scanxy_1_p11, vgasync_1_p19,
       vgasync_1_p20, vgasync_1_p21, vgasync_1_p22, vgasync_1_p23;
  wire [11:0] vgasync_1_p17, vgasync_1_p18;

  // scanxy scanxy_1: pin names not known; wires that end beside it: clk, rst, 1'b1, httl, vttl, scanxy_1_p6, scanxy_1_p7, scanxy_1_p8, scanxy_1_p9, scanxy_1_p10, scanxy_1_p11
  // vgasync vgasync_1: pin names not known; wires that end beside it: clk, rst, scanxy_1_p6, scanxy_1_p7, scanxy_1_p8, scanxy_1_p9, scanxy_1_p10, scanxy_1_p11, hfp, hsn, hbp, hneg, vfp, vsn, vbp, vneg, vgasync_1_p17, vgasync_1_p18, vgasync_1_p19, vgasync_1_p20, vgasync_1_p21, vgasync_1_p22, vgasync_1_p23
  engine engine_1 (
    .clk(clk), .rst(rst), .x_i(vgasync_1_p17), .y_i(vgasync_1_p18), .nl_i(vgasync_1_p19),
    .nf_i(vgasync_1_p20), .hs_i(vgasync_1_p21), .vs_i(vgasync_1_p22), .de_i(vgasync_1_p23), .x_o(X), .y_o(Y),
    .nl_o(nl), .nf_o(nf), .r(R), .g(G), .b(B), .hs_o(hs), .vs_o(vs), .de_o(de));

  // Other names for the same wires on the sheet: C = clk; R_t = rst

  // Notes on the sheet:
  //   clk: Hz: 2147483647
  //   hfp: default 3
  //   hsn: default 5
  //   hbp: default 5
  //   vfp: default 3
  //   vsn: default 5
  //   vbp: default 5
endmodule
