// Digital circuit vgasync.dig as structural Verilog
module vgasync (
  input  clk,
  input  rst,
  input  [11:0] nx,
  input  [11:0] ny,
  input  [11:0] x_i,
  input  [11:0] y_i,
  input  nl_i,
  input  nf_i,
  input  [11:0] hfp,
  input  [11:0] hsn,
  input  [11:0] hbp,
  input  hneg,
  input  [11:0] vfp,
  input  [11:0] vsn,
  input  [11:0] vbp,
  input  vneg,
  output [11:0] x_o,
  output [11:0] y_o,
  output nl_o,
  output nf_o,
  output hs,
  output vs,
  output de
);

  wire undriven, undriven_2;

  sync H (
    .clk(clk), .rst(rst), .v(nx), .fp(hfp), .sync(hsn), .bp(hbp), .n(nl_i), .neg(hneg), .pulse(hs));  // open: blank
  sync V (.clk(clk), .rst(rst), .v(ny), .fp(vfp), .sync(vsn), .bp(vbp), .n(nf_i), .neg(vneg));  // open: blank, pulse
  nor nor_1 (de, undriven, undriven_2);

  assign nf_o = nf_i;
  assign nl_o = nl_i;
  assign x_o = x_i;
  assign y_o = y_i;

  // Other names for the same wires on the sheet: C = clk; nf_t = nf_i; nl_t = nl_i; R = rst

  // Notes on the sheet:
  //   hfp: default 3
  //   hsn: default 5
  //   hbp: default 5
  //   vfp: default 3
  //   vsn: default 5
  //   vbp: default 5
endmodule
