// Digital circuit vga_blinkenlights.dig as structural Verilog
module vga_blinkenlights (
  input  clock,
  input  [25:0] db,
  input  [15:0] TD,
  input  [7:0] MD,
  output [3:0] R,
  output [3:0] G,
  output [3:0] B,
  output hs,
  output vs,
  output de,
  output [10:0] TA,
  output [9:0] MA
);

  wire error_t, halt_t, immv_t, jump_p13, jump_p14, jump_p15, jump_p16, jump_t, L_v, PC_p14, PC_p15, PC_p16,
       PC_p17, R0_p14, R0_p15, R0_p16, R0_p17, R1_p14, R1_p15, R1_p16, R1_p17, R_v, rdv_t, res_v, rsv_t,
       skip_p13, skip_p14, skip_p15, skip_p16, skip_t, vb;
  wire [2:0] aluop_t, cond_t;
  wire [3:0] error_fg_o, halt_p16, L_p4, L_p17, Op_fg_o, R2_p17, R3_fg_o, R_fg_o, rd_2_fg_o, rd_fg_o, rd_t,
       result_2_fg_o, result_fg_o, rs_fg_o, rs_t;
  wire [4:0] op_t;
  wire [6:0] error_c_o, halt_p15, L_p3, L_p16, Op_c_o, R2_p16, R3_c_o, R_c_o, rd_2_c_o, rd_c_o, result_2_c_o,
       result_c_o, rs_c_o;
  wire [7:0] error_cx_o, error_cy_o, halt_p13, halt_p14, L_p1, L_p2, L_p14, L_p15, Op_cx_o, Op_cy_o, R2_p14,
       R2_p15, R3_cx_o, R3_cy_o, R_cx_o, R_cy_o, rd_2_cx_o, rd_2_cy_o, rd_cx_o, rd_cy_o, result_cx_o,
       result_cy_o, rs_cx_o, rs_cy_o, vga_display_1_cx, vga_display_1_cy;
  wire [15:0] debugcopy_1_ctrl, debugcopy_1_decode, imm_t, L_t, PC_t, R0_t, R1_t, R2_t, R3_t, R_t, result_t;

  debugcopy debugcopy_1 (
    .db(db), .clock(clock), .e(vb), .R0(R0_t), .R1(R1_t), .R2(R2_t), .R3(R3_t), .decode(debugcopy_1_decode),
    .ctrl(debugcopy_1_ctrl), .L(L_t), .R(R_t), .result(result_t), .imm(imm_t), .pc(PC_t));
  ctrldec ctrldec_1 (
    .ctrl(debugcopy_1_ctrl), .skip(skip_t), .halt(halt_t), .error(error_t), .jump(jump_t), .aluop(aluop_t),
    .rdvalid(rdv_t), .rsvalid(rsv_t), .immv(immv_t));  // open: stall, mem, store, write, en_fetch, en
  decodedec decodedec_1 (.D(debugcopy_1_decode), .op(op_t), .cond(cond_t), .rs(rs_t), .rd(rd_t));
  vga_display vga_display_1 (
    .clock(clock), .res_H(12'h280), .fp_H(12'h10), .sync_H(12'h60), .bp_H(12'h30), .neg_H(1'b1),
    .res_V(12'h1e0), .fp_V(12'ha), .sync_V(12'h2), .bp_V(12'h22), .neg_V(1'b1), .char(result_2_c_o),
    .fg(result_2_fg_o), .bg(12'h112), .TD(TD), .MD(MD), .R(R), .G(G), .B(B), .hs(hs), .vs(vs), .de(de),
    .CX(vga_display_1_cx), .CY(vga_display_1_cy), .vblank(vb), .TA(TA), .MA(MA));  // open: hblank
  // vga_labelnum L: pin names not known; wires that end beside it: L_p1, L_p2, L_p3, L_p4, 4'b0001, 4'b0010, 5'b00010, 8'hc, L_v, 7'b0100000, 7'b0111101, 7'b0100000, L_t, L_p14, L_p15, L_p16, L_p17
  vga_opdisp Op (
    .CX_i(L_p14), .CY_i(L_p15), .C_i(L_p16), .fg_i(L_p17), .fg_c(4'b0101), .CX_c(5'b00001), .CY_c(8'hb),
    .en(1'b1), .op(op_t), .cond(cond_t), .CX_o(Op_cx_o), .CY_o(Op_cy_o), .C_o(Op_c_o), .fg_o(Op_fg_o));
  // vga_labelnum PC: pin names not known; wires that end beside it: vga_display_1_cx, vga_display_1_cy, {7{1'b0}}, 4'b0000, 4'b0001, 4'b0010, 5'b00001, 8'h8, 1'b1, 7'b0100000, 7'b1010000, 7'b1000011, PC_t, PC_p14, PC_p15, PC_p16, PC_p17
  vga_hex u_R (
    .CX_i(Op_cx_o), .CY_i(Op_cy_o), .C_i(Op_c_o), .fg_i(Op_fg_o), .fg_c(4'b0010), .CX_c(6'b000111),
    .CY_c(8'hc), .N(R_t), .en(R_v), .CX_o(R_cx_o), .CY_o(R_cy_o), .C_o(R_c_o), .fg_o(R_fg_o));
  // vga_labelnum R0: pin names not known; wires that end beside it: PC_p14, PC_p15, PC_p16, PC_p17, 4'b0001, 4'b0010, 5'b00011, 8'h2, 1'b1, 7'b0100000, 7'b1010010, 7'b0110000, R0_t, R0_p14, R0_p15, R0_p16, R0_p17
  vga_hex result (
    .CX_i(R_cx_o), .CY_i(R_cy_o), .C_i(R_c_o), .fg_i(R_fg_o), .fg_c(4'b0010), .CX_c(6'b000011), .CY_c(8'hc),
    .N(result_t), .en(res_v), .CX_o(result_cx_o), .CY_o(result_cy_o), .C_o(result_c_o), .fg_o(result_fg_o));
  // vga_labelnum R1: pin names not known; wires that end beside it: R0_p14, R0_p15, R0_p16, R0_p17, 4'b0001, 4'b0010, 5'b00011, 8'h3, 1'b1, 7'b0100000, 7'b1010010, 7'b0110001, R1_t, R1_p14, R1_p15, R1_p16, R1_p17
  // vga_string jump: pin names not known; wires that end beside it: result_cx_o, result_cy_o, result_c_o, result_fg_o, 4'b0001, 6'b000010, 8'h7, 7'b1001010, 7'b1010101, 7'b1001101, 7'b1010000, jump_t, jump_p13, jump_p14, jump_p15, jump_p16
  // vga_labelnum R2: pin names not known; wires that end beside it: R1_p14, R1_p15, R1_p16, R1_p17, 4'b0001, 4'b0010, 5'b00011, 8'h4, 1'b1, 7'b0100000, 7'b1010010, 7'b0110010, R2_t, R2_p14, R2_p15, R2_p16, R2_p17
  // vga_string skip: pin names not known; wires that end beside it: jump_p13, jump_p14, jump_p15, jump_p16, 4'b0011, 6'b000011, 8'h7, 7'b1010011, 7'b1001011, 7'b1001001, 7'b1010000, skip_t, skip_p13, skip_p14, skip_p15, skip_p16
  vga_labelnum R3 (
    .CX_i(R2_p14), .CY_i(R2_p15), .C_i(R2_p16), .fg_i(R2_p17), .fg_lab(4'b0001), .fg_num(4'b0010),
    .CX_c(5'b00011), .CY_c(8'h5), .en(1'b1), .L_0(7'b0100000), .L_1(7'b1010010), .L_2(7'b0110011), .N(R3_t),
    .CX_o(R3_cx_o), .CY_o(R3_cy_o), .C_o(R3_c_o), .fg_o(R3_fg_o));
  // vga_string halt: pin names not known; wires that end beside it: skip_p13, skip_p14, skip_p15, skip_p16, 4'b0100, 6'b000010, 8'h2, 7'b1001000, 7'b1000001, 7'b1001100, 7'b1010100, halt_t, halt_p13, halt_p14, halt_p15, halt_p16
  vga_regdisp rd (
    .CX_i(R3_cx_o), .CY_i(R3_cy_o), .C_i(R3_c_o), .fg_i(R3_fg_o), .fg_c(4'b0001), .CX_c(6'b000101),
    .CY_c(8'hb), .en(rdv_t), .R(rd_t), .J(jump_t), .sep(7'b0101100), .CX_o(rd_cx_o), .CY_o(rd_cy_o),
    .C_o(rd_c_o), .fg_o(rd_fg_o));
  vga_string error (
    .CX_i(halt_p13), .CY_i(halt_p14), .C_i(halt_p15), .fg_i(halt_p16), .fg_c(4'b0010), .CX_c(6'b000011),
    .CY_c(8'h2), .C_0(7'b1000101), .C_1(7'b1010010), .C_2(7'b1010010), .C_3(7'b1000100), .en(error_t),
    .CX_o(error_cx_o), .CY_o(error_cy_o), .C_o(error_c_o), .fg_o(error_fg_o));
  vga_regdisp rs (
    .CX_i(rd_cx_o), .CY_i(rd_cy_o), .C_i(rd_c_o), .fg_i(rd_fg_o), .fg_c(4'b0001), .CX_c(6'b000110),
    .CY_c(8'hb), .en(rsv_t), .R(rs_t), .J(1'b0), .sep(7'b0100000), .CX_o(rs_cx_o), .CY_o(rs_cy_o),
    .C_o(rs_c_o), .fg_o(rs_fg_o));
  vga_regdisp rd_2 (
    .CX_i(error_cx_o), .CY_i(error_cy_o), .C_i(error_c_o), .fg_i(error_fg_o), .fg_c(4'b0001),
    .CX_c(6'b000010), .CY_c(8'hc), .en(res_v), .R(rd_t), .J(jump_t), .sep(7'b0111101), .CX_o(rd_2_cx_o),
    .CY_o(rd_2_cy_o), .C_o(rd_2_c_o), .fg_o(rd_2_fg_o));
  vga_aluopdisp aluop (
    .CX_i(rs_cx_o), .CY_i(rs_cy_o), .C_i(rs_c_o), .fg_i(rs_fg_o), .fg_c(4'b0011), .CX_c(6'b000110),
    .CY_c(8'hc), .en(1'b1), .aop(aluop_t), .CX_o(L_p1), .CY_o(L_p2), .C_o(L_p3), .fg_o(L_p4), .L_v(L_v),
    .R_v(R_v), .res_v(res_v));
  vga_hex result_2 (
    .CX_i(rd_2_cx_o), .CY_i(rd_2_cy_o), .C_i(rd_2_c_o), .fg_i(rd_2_fg_o), .fg_c(4'b0010), .CX_c(6'b000111),
    .CY_c(8'hb), .N(imm_t), .en(immv_t), .C_o(result_2_c_o), .fg_o(result_2_fg_o));  // open: CX_o, CY_o

  // Other names for the same wires on the sheet: C = clock

  // Notes on the sheet:
  //   clock: Hz: 2147483647
endmodule
