// Digital circuit vga_display.dig as structural Verilog
module vga_display (
  input  clock,
  input  [11:0] res_H,
  input  [11:0] fp_H,
  input  [11:0] sync_H,
  input  [11:0] bp_H,
  input  neg_H,
  input  [11:0] res_V,
  input  [11:0] fp_V,
  input  [11:0] sync_V,
  input  [11:0] bp_V,
  input  neg_V,
  input  [6:0] char,
  input  [3:0] fg,
  input  [11:0] bg,
  input  [15:0] TD,
  input  [7:0] MD,
  output [3:0] R,
  output [3:0] G,
  output [3:0] B,
  output hs,
  output vs,
  output de,
  output [7:0] CX,
  output [7:0] CY,
  output vblank,
  output hblank,
  output [10:0] TA,
  output [9:0] MA
);

  wire vga_sync_1_p12, vga_sync_1_p13, vga_sync_1_p14;
  wire [3:0] vga_charpos_1_col;
  wire [4:0] vga_charpos_1_row;
  wire [11:0] vga_sync_1_p15, vga_sync_1_p16;

  // vga_sync vga_sync_1: pin names not known; wires that end beside it: clock, res_H, bp_H, sync_H, fp_H, neg_H, res_V, bp_V, sync_V, fp_V, neg_V, vga_sync_1_p12, vga_sync_1_p13, vga_sync_1_p14, vga_sync_1_p15, vga_sync_1_p16, hblank, vblank
  vga_charpos vga_charpos_1 (
    .X(vga_sync_1_p15), .Y(vga_sync_1_p16), .row(vga_charpos_1_row), .col(vga_charpos_1_col), .CX(CX), .CY(CY));
  vga_text vga_text_1 (
    .H_i(vga_sync_1_p12), .V_i(vga_sync_1_p13), .pic(vga_sync_1_p14), .row(vga_charpos_1_row),
    .col(vga_charpos_1_col), .TD(TD), .MD(MD), .clock(clock), .char(char), .fg(fg), .bg(bg), .R(R), .G(G),
    .B(B), .hs(hs), .vs(vs), .de(de), .TA(TA), .MA(MA));

  // Other names for the same wires on the sheet: C = clock

  // Notes on the sheet:
  //   clock: Hz: 2147483647
  //   res_H: default 640
  //   fp_H: default 16
  //   sync_H: default 96
  //   bp_H: default 48
  //   res_V: default 640
  //   fp_V: default 16
  //   sync_V: default 96
  //   bp_V: default 48
endmodule
