// Digital circuit vga_text.dig as structural Verilog
module vga_text (
  input  H_i,
  input  V_i,
  input  pic,
  input  [4:0] row,
  input  [3:0] col,
  input  [15:0] CD,
  input  clock,
  input  [6:0] char,
  input  [11:0] fg,
  input  [11:0] bg,
  output [3:0] R,
  output [3:0] G,
  output [3:0] B,
  output hs,
  output vs,
  output de,
  output [10:0] CA
);

  wire sub_1_c_o;
  wire [0:0] multiplexer_2_out;
  wire [3:0] d_ff_3_q;
  wire [6:0] sub_1_s;
  wire [11:0] d_ff_5_q, d_ff_6_q;

  Sub #(.Bits(7)) sub_1 (.a(char), .b(7'b0100000), .c_i(1'b0), .s(sub_1_s), .c_o(sub_1_c_o));
  Multiplexer #(.Bits(6)) multiplexer_1 (.sel(sub_1_c_o), .in_0(sub_1_s[5:0]), .in_1({6{1'b0}}), .out(CA[10:5]));
  D_FF d_ff_1 (.D(H_i), .C(clock), .Q(hs));  // open: nQ
  D_FF d_ff_2 (.D(V_i), .C(clock), .Q(vs));  // open: nQ
  D_FF #(.Bits(4)) d_ff_3 (.D(col), .C(clock), .Q(d_ff_3_q));  // open: nQ
  D_FF d_ff_4 (.D(pic), .C(clock), .Q(de));  // open: nQ
  D_FF #(.Bits(12)) d_ff_5 (.D(bg), .C(clock), .Q(d_ff_5_q));  // open: nQ
  D_FF #(.Bits(12)) d_ff_6 (.D(fg), .C(clock), .Q(d_ff_6_q));  // open: nQ
  Multiplexer #(.Selector_Bits(4)) multiplexer_2 (
    .sel(d_ff_3_q), .in_0(CD[15]), .in_1(CD[14]), .in_2(CD[13]), .in_3(CD[12]), .in_4(CD[11]), .in_5(CD[10]),
    .in_6(CD[9]), .in_7(CD[8]), .in_8(CD[7]), .in_9(CD[6]), .in_10(CD[5]), .in_11(CD[4]), .in_12(CD[3]),
    .in_13(CD[2]), .in_14(CD[1]), .in_15(CD[0]), .out(multiplexer_2_out[0]));
  Multiplexer #(.Selector_Bits(2), .Bits(12)) multiplexer_3 (
    .sel({de, multiplexer_2_out[0]}), .in_0({12{1'b0}}), .in_1({12{1'b0}}), .in_2(d_ff_5_q), .in_3(d_ff_6_q),
    .out({R, G, B}));

  assign CA[4:0] = row;

  // Other names for the same wires on the sheet: C = clock
endmodule
