// Digital circuit vgafp.dig as structural Verilog
module vgafp (
  input  clk
);

  wire vga_display_1_p3, vga_display_1_p4, vga_display_1_p5, vga_display_1_p6, vga_display_1_p7;
  wire [10:0] vga_display_1_p8;
  wire [15:0] Char_ROM_d, vga_display_1_p2;

  // vga_display vga_display_1: pin names not known; wires that end beside it: clk, vga_display_1_p2, vga_display_1_p3, vga_display_1_p4, vga_display_1_p5, vga_display_1_p6, vga_display_1_p7, vga_display_1_p8
  VGA vga_1 (
    .R(vga_display_1_p3), .G(vga_display_1_p4), .B(vga_display_1_p5), .H(vga_display_1_p6),
    .V(vga_display_1_p7), .C(clk));
  ROM #(.AddrBits(11), .Bits(16)) Char_ROM (.A(vga_display_1_p8), .sel(1'b1), .D(Char_ROM_d));
  D_FF #(.Bits(16)) d_ff_1 (.D(Char_ROM_d), .C(clk), .Q(vga_display_1_p2));  // open: nQ

  // Other names for the same wires on the sheet: C = clk

  // Notes on the sheet:
  //   clk: Hz: 2147483647
  //   contents of Char_ROM (hex, n*v repeats v):
  //   0,0,0,0,0,0,0,0,0,0,0,0,0,0,0,0,0,0,0,0,0,0,0,0,0,0,0,0,0,0,0,0,0,0,0,180,180,180,
  //   180,180,180,180,180,0,0,180,180,180,180,180,180,180,180,0,0,0,0,0,0,0,0,0,0,0,0,3e7c,
  //   1e78,0,0,0,0,0,0,0,0,0,0,0,0,0,0,0,0,0,0,0,0,0,0,0,0,0,0,0,0,0,0,3e7c,3ffc,4182,6186,
  //   6186,6186,6186,6186,6186,4182,3e7c,3e7c,4182,6186,6186,6186,6186,6186,6186,4182,3ffc,
  //   3e7c,0,0,0,0,0,0,0,0,0,0,3e7c,3ff8,4180,6180,6180,6180,6180,6180,6180,4180,3e7c,3e7c,
  //   182,186,186,186,186,186,186,182,1ffc,3e7c,0,0,0,0,0,0,0,0,0,0,3e00,3f00,4188,6188,
  //   6198,61b0,61b0,61e0,61e0,4180,3e7c,3e7c,182,786,786,d86,d86,1986,1186,1182,fc,7c,
  //   0,0,0,0,0,0,0,0,0,0,3e00,3f00,4180,6180,6180,6180,6180,6180,6180,4180,3f00,3e00,4000,
  //   6060,6060,6030,6030,6018,6008,4000,3e78,3e7c,0,0,0,0,0,0,0,0,0,0,0,0,8,8,18,30,30,
  //   60,60,0,0,0,0,0,0,0,0,0,0,0,0,0,0,0,0,0,0,0,0,0,0,0,7c,78,200,600,600,c00,800,1800,
  //   1000,0,0,0,0,1000,1800,800,c00,600,600,200,78,7c,0,0,0,0,0,0,0,0,0,0,3e00,1e00,40,
  //   60,60,30,10,18,8,0,0,0,0,8,18,10,30,60,60,40,1e00,3e00,0,0,0,0,0,0,0,0,0,0,0,0,1188,
  //   1188,1998,db0,db0,7e0,7e0,180,3e7c,3e7c,180,7e0,7e0,db0,db0,1998,1188,1188,0,0,0,
  //   0,0,0,0,0,0,0,0,0,0,0,180,180,180,180,180,180,180,180,3e7c,3e7c,180,180,180,180,180,
  //   180,180,180,0,0,0,0,0,0,0,0,0,0,0,0,0,0,0,0,0,0,0,0,0,0,0,0,0,600,600,c00,c00,1800,
  //   1000,1000,0,0,0,0,0,0,0,0,0,0,0,0,0,0,0,0,0,0,0,0,0,0,3e7c,3e7c,0,0,0,0,0,0,0,0,0,
  //   0,0,0,0,0,0,0,0,0,0,0,0,0,0,0,0,0,0,0,0,0,0,0,0,0,0,0,0,0,0,0,180,180,0,0,0,0,0,0,
  //   0,0,0,0,0,0,8,8,18,30,30,60,60,0,0,0,0,600,600,c00,c00,1800,1000,1000,0,0,0,0,0,0,
  //   0,0,0,0,0,0,3e7c,3e7c,4006,600e,601a,6032,6036,6066,6066,6006,0,0,6006,6606,6606,
  //   6c06,4c06,5806,7006,6002,3e7c,3e7c,0,0,0,0,0,0,0,0,0,0,3e00,1f00,180,180,180,180,
  //   180,180,180,180,0,0,180,180,180,180,180,180,180,180,1ff8,3e7c,0,0,0,0,0,0,0,0,0,0,
  //   3e7c,1e7c,2,6,6,6,6,6,6,2,3e7c,3e7c,4000,6000,6000,6000,6000,6000,6000,4000,3e78,
  //   3e7c,0,0,0,0,0,0,0,0,0,0,3e7c,1e7c,2,6,6,6,6,6,6,2,3e7c,3e7c,2,6,6,6,6,6,6,2,1e7c,
  //   3e7c,0,0,0,0,0,0,0,0,0,0,0,4002,6006,6006,6006,6006,6006,6006,6006,4002,3e7c,3e7c,
  //   2,6,6,6,6,6,6,6,2,0,0,0,0,0,0,0,0,0,0,0,3e7c,3e78,4000,6000,6000,6000,6000,6000,6000,
  //   4000,3e7c,3e7c,2,6,6,6,6,6,6,2,1e7c,3e7c,0,0,0,0,0,0,0,0,0,0,3e7c,3e78,4000,6000,
  //   6000,6000,6000,6000,6000,4000,3e7c,3e7c,4002,6006,6006,6006,6006,6006,6006,4002,3e7c,
  //   3e7c,0,0,0,0,0,0,0,0,0,0,3e7c,1e7c,2,6,6,6,6,6,6,6,0,0,6,6,6,6,6,6,6,6,2,0,0,0,0,
  //   0,0,0,0,0,0,0,3e7c,3e7c,4002,6006,6006,6006,6006,6006,6006,4002,3e7c,3e7c,4002,6006,
  //   6006,6006,6006,6006,6006,4002,3e7c,3e7c,0,0,0,0,0,0,0,0,0,0,3e7c,3e7c,4002,6006,6006,
  //   6006,6006,6006,6006,4002,3e7c,3e7c,2,6,6,6,6,6,6,2,1e7c,3e7c,0,0,0,0,0,0,0,0,0,0,
  //   0,0,0,0,0,180,180,0,0,0,0,0,0,0,0,180,180,0,0,0,0,0,0,0,0,0,0,0,0,0,0,0,0,0,180,180,
  //   180,180,180,180,180,180,0,0,0,600,600,c00,c00,1800,1000,1000,0,0,0,0,0,0,0,0,0,0,
  //   0,0,0,0,40,c0,c0,180,180,300,300,0,0,0,0,300,300,180,180,c0,c0,40,0,0,0,0,0,0,0,0,
  //   0,0,0,0,0,0,0,0,0,3e7c,3e7c,0,0,0,0,0,0,0,0,1e78,3e7c,0,0,0,0,0,0,0,0,0,0,0,0,0,0,
  //   0,0,0,200,300,300,180,180,c0,c0,0,0,0,0,c0,c0,180,180,300,300,200,0,0,0,0,0,0,0,0,
  //   0,0,0,0,3e7c,1e7c,2,6,6,6,6,6,6,2,7c,fc,180,180,180,180,180,180,180,180,0,0,0,0,0,
  //   0,0,0,0,0,0,0,3e7c,3ffc,4182,6186,6186,6186,6186,6186,6186,6182,fc,7c,6000,6000,6000,
  //   6000,6000,6000,6000,4000,3e78,3e7c,0,0,0,0,0,0,0,0,0,0,3e7c,3e7c,4002,6006,6006,6006,
  //   6006,6006,6006,4002,3e7c,3e7c,4002,6006,6006,6006,6006,6006,6006,6006,4002,0,0,0,
  //   0,0,0,0,0,0,0,0,3e7c,1ffc,182,186,186,186,186,186,186,182,3e7c,3e7c,182,186,186,186,
  //   186,186,186,182,1ffc,3e7c,0,0,0,0,0,0,0,0,0,0,3e7c,3e78,4000,6000,6000,6000,6000,
  //   6000,6000,6000,0,0,6000,6000,6000,6000,6000,6000,6000,4000,3e78,3e7c,0,0,0,0,0,0,
  //   0,0,0,0,3e7c,1ffc,182,186,186,186,186,186,186,186,0,0,186,186,186,186,186,186,186,
  //   182,1ffc,3e7c,0,0,0,0,0,0,0,0,0,0,3e7c,3e78,4000,6000,6000,6000,6000,6000,6000,4000,
  //   3e7c,3e7c,4000,6000,6000,6000,6000,6000,6000,4000,3e78,3e7c,0,0,0,0,0,0,0,0,0,0,3e7c,
  //   3e78,4000,6000,6000,6000,6000,6000,6000,4000,3e7c,3e7c,4000,6000,6000,6000,6000,6000,
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endmodule
